// Logisim project 7SegDisp.circ as structural Verilog
module _7SegDisp4In (
  input  I0,
  input  I1,
  input  I2,
  input  I3
);

  wire and_1_out, and_2_out, and_3_out, and_4_out, and_5_out, and_6_out, and_7_out, and_8_out, and_9_out,
       and_10_out, and_11_out, and_12_out, and_13_out, and_14_out, and_15_out, and_16_out, not_1_out,
       not_2_out, not_3_out, not_4_out, not_5_out, not_6_out, not_7_out, not_8_out, not_9_out, not_10_out,
       not_11_out, not_12_out, not_13_out, not_14_out, not_15_out, not_16_out, not_17_out, not_18_out,
       not_19_out, not_20_out, not_21_out, or_1_out, or_2_out, or_3_out, or_4_out, or_5_out, or_6_out,
       or_7_out;

  not not_1 (not_1_out, I1);
  and and_1 (and_1_out, not_1_out, not_2_out);
  not not_2 (not_2_out, I3);
  and and_2 (and_2_out, I1, I3);
  not not_3 (not_3_out, I1);
  not not_4 (not_4_out, I2);
  and and_3 (and_3_out, not_4_out, not_5_out);
  not not_5 (not_5_out, I3);
  and and_4 (and_4_out, I2, I3);
  not not_6 (not_6_out, I2);
  or or_1 (or_1_out, not_6_out, I3, I1);
  not not_7 (not_7_out, I1);
  and and_5 (and_5_out, not_7_out, not_8_out);
  not not_8 (not_8_out, I3);
  not not_9 (not_9_out, I1);
  and and_6 (and_6_out, not_9_out, I2);
  and and_7 (and_7_out, I2, not_10_out);
  not not_10 (not_10_out, I3);
  and and_8 (and_8_out, I1, not_11_out, I3);
  not not_11 (not_11_out, I2);
  not not_12 (not_12_out, I1);
  and and_9 (and_9_out, not_12_out, not_13_out);
  not not_13 (not_13_out, I3);
  and and_10 (and_10_out, I2, not_14_out);
  not not_14 (not_14_out, I3);
  not not_15 (not_15_out, I2);
  and and_11 (and_11_out, not_15_out, not_16_out);
  not not_16 (not_16_out, I3);
  and and_12 (and_12_out, I1, not_17_out);
  not not_17 (not_17_out, I2);
  and and_13 (and_13_out, I1, not_18_out);
  not not_18 (not_18_out, I3);
  not not_19 (not_19_out, I1);
  and and_14 (and_14_out, not_19_out, I2);
  and and_15 (and_15_out, I1, not_20_out);
  not not_20 (not_20_out, I2);
  and and_16 (and_16_out, I1, not_21_out);
  not not_21 (not_21_out, I3);
  or or_2 (or_2_out, and_1_out, I2, and_2_out, I0);
  or or_3 (or_3_out, not_3_out, and_3_out, and_4_out);
  or or_4 (or_4_out, and_5_out, and_6_out, and_7_out, and_8_out, I0);
  or or_5 (or_5_out, and_9_out, and_10_out);
  or or_6 (or_6_out, and_11_out, and_12_out, and_13_out, I0);
  or or_7 (or_7_out, and_14_out, and_15_out, and_16_out, I0);
  _7_Segment_Display u_7_segment_display_1 (
    .g(or_7_out), .f(or_6_out), .a(or_2_out), .b(or_3_out), .e(or_5_out), .d(or_4_out), .c(or_1_out));  // open: dp
endmodule

module _7SegDisp4In3 (
  input  I0,
  input  I1,
  input  I2,
  input  I3
);

  wire and_1_out, and_2_out, not_1_out, not_2_out, not_3_out, not_4_out, not_5_out, not_6_out, or_1_out,
       or_2_out, or_3_out, or_4_out, or_5_out, or_6_out;

  not not_1 (not_1_out, I3);
  or or_1 (or_1_out, not_1_out, I2);
  not not_2 (not_2_out, I2);
  or or_2 (or_2_out, not_2_out, I3, I1);
  not not_3 (not_3_out, I3);
  or or_3 (or_3_out, not_3_out, I2);
  not not_4 (not_4_out, I3);
  or or_4 (or_4_out, not_4_out, I2);
  not not_5 (not_5_out, I2);
  and and_1 (and_1_out, not_5_out, not_6_out);
  not not_6 (not_6_out, I3);
  and and_2 (and_2_out, I2, I3);
  or or_5 (or_5_out, I2, I1);
  or or_6 (or_6_out, and_1_out, and_2_out);
  _7_Segment_Display u_7_segment_display_1 (
    .g(or_5_out), .f(or_6_out), .a(or_1_out), .b(1'b1), .e(or_4_out), .d(or_3_out), .c(or_2_out));  // open: dp
endmodule

module _7Seg2In3 (
  input  I0,
  input  I1
);

  wire and_1_out, not_1_out, not_2_out, not_3_out, not_4_out, not_5_out, not_6_out, or_1_out, or_2_out,
       or_3_out;

  not not_1 (not_1_out, I1);
  not not_2 (not_2_out, I0);
  not not_3 (not_3_out, I1);
  not not_4 (not_4_out, I1);
  not not_5 (not_5_out, I0);
  not not_6 (not_6_out, I1);
  or or_1 (or_1_out, not_1_out, I0);
  or or_2 (or_2_out, not_2_out, I1);
  or or_3 (or_3_out, not_3_out, I0);
  and and_1 (and_1_out, not_5_out, not_6_out);
  _7_Segment_Display u_7_segment_display_1 (
    .g(I0), .f(and_1_out), .a(or_1_out), .b(1'b1), .e(not_4_out), .d(or_3_out), .c(or_2_out));  // open: dp
endmodule
